# Fritzing sketch DiveIno (saved by Fritzing 0.9.3b)
breadboards: 2

parts:
  Main_Board = Arduino Mega 2560 (Rev3)
  RTC = Adafruit DS3231 [part_number="Adafruit #3013"]
  On/Off = Toggle Switch [package=THT]
  Speaker = Piezo Speaker
  Infra = TSOP312.., 314.. [package=THT]
  Power = female pin header, 3 pins [form="♀ (female)"]
  Reed = Reed switch [package=THT]
  Bluefruit = Adafruit Bluefruit LE UART Friend [part_number="Adafruit #2479"]
  Transistor = NPN-Transistor [package="TO92 [THT]"]
  Base = Resistor [tolerance=±5% resistance=250k package=THT]
  Water = Resistor [tolerance=±5% resistance=100k package=THT]
  Data = female pin header, 4 pins [form="♀ (female)"]
  Water_LED = LED - 5mm [color="Blue (430nm)" package="5 mm [THT]"]
  LED = Resistor [tolerance=±5% resistance=220 package=THT]
  Control = female pin header, 4 pins [form="♀ (female)"]
  Reed_2 = Resistor [tolerance=±5% resistance=10k package=THT]
  Reed_3 = female pin header, 2 pins [form="♀ (female)"]
  Switch = female pin header, 4 pins [form="♀ (female)"]
  Emitter = Resistor [tolerance=±5% resistance=220 package=THT]
  Fuel_Gauge = SparkFun LiPo Fuel Gauge [part_number=TOL-10617]
  Pressure_Sensor = SparkFun Pressure Sensor Breakout - MS5803-14BA [part_number="SEN-12909 "]
  Charger = PowerBoost 500 Charger

nets:
  N1: Main_Board.D11_PWM, Infra.GND, Control.pin1
  N2: Main_Board.D8_PWM, Speaker.pin2, Control.pin2
  VIN: Main_Board.3V3, RTC.Vin, Infra.Data, Power.pin1, Bluefruit.VIN, Bluefruit.RXI, Water.Pin_0, Data.pin1, Emitter.Pin_0, Pressure_Sensor.3.3V
  GND: Main_Board.GND, RTC.GND, Speaker.pin1, Infra.Vs, Power.pin2, Bluefruit.GND, Bluefruit.CTS, Transistor.C, Base.Pin_0, Water_LED.cathode, Fuel_Gauge.QST, Fuel_Gauge.GND, Pressure_Sensor.GND
  N3: Main_Board.VIN, Power.pin3, Charger.5.0V
  N4: Main_Board.D3_PWM, Transistor.E, Control.pin4, Emitter.Pin_1
  N5: Main_Board.D6_PWM, LED.Pin_0, Control.pin3
  N6: RTC.SCL, Data.pin4, Fuel_Gauge.SCL, Pressure_Sensor.SCL/SCLK
  N7: RTC.SDA, Data.pin3, Fuel_Gauge.SDA, Pressure_Sensor.SDA/SDI
  N8: On/Off.COM, Reed.pin_2, Reed_2.Pin_0, Reed_3.pin1, Switch.pin4, Charger.ENABLE
  N9: On/Off.L2, Reed.pin_1, Reed_3.pin2, Switch.pin3, Charger.GND
  N10: Bluefruit.TXO, Data.pin2
  N11: Transistor.B, Base.Pin_1, Switch.pin1
  N12: Water.Pin_1, Switch.pin2
  N13: Water_LED.anode, LED.Pin_1
  N14: Reed_2.Pin_1, Fuel_Gauge.VCC, Charger.VBAT

notes:
  DiveIno

custom parts:
  Adafruit DS3231: The datasheet for the DS3231 explains that this part is an "Extremely Accurate I²C-Integrated RTC/TCXO/Crystal". And, hey, it does exactly what it says on the tin! This Real Time Clock (RTC) is the most precise you can get in a small, low power package. Most RTCs use an external 32kHz timing crystal that is used to keep time with low current draw. And that's all well and good, but those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
  Adafruit Bluefruit LE UART Friend: The Bluefruit LE UART Friend makes it easy to add Bluetooth Low Energy connectivity to anything with a hardware or software serial port. We even have nice hardware flow control so you won't have to think about losing data. Connect to your Arduino or other microcontroller or even just a standard FTDI cable for debugging and testing.
  SparkFun LiPo Fuel Gauge: LiPo batteries are a great way to power your projects. They’re small, lightweight, and pack a pretty good punch for their size. Unfortunately, even the best batteries eventually run low on power and when they do it’s often unexpected (and at the worst time). Don’t be caught by surprise next time your board suddenly powers-down! The SparkFun LiPo Fuel Gauge connects your battery to your project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
  SparkFun Pressure Sensor Breakout - MS5803-14BA: This is the MS5803-14BA Pressure Sensor Breakout, a high resolution pressure sensor with both an I2C and SPI interface. This MEMS pressure sensor measures the absolute pressure of the fluid around it which includes air, water, and anything else that acts like a viscous fluid. Depending on how you interpret the data, you can determine altitude, water depth, or any other tasks that require an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
  PowerBoost 500 Charger: The PowerBoost 500C is a little DC/DC boost converter module that can be powered by any 3.7V LiIon/LiPoly battery, and convert the battery output to 5.2V DC for running your 5V projects. At its heart is a TPS61090 boost converter from TI. This boost converter chip has some really nice extras such as low battery detection, 2A internal switch, synchronous conversion, excellent efficiency, and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
