# Fritzing sketch PowerModule (saved by Fritzing 0.9.3b)
circuit board: 4cm x 5cm
breadboards: 1

parts:
  LiPo_Fuel_Gauge = SparkFun LiPo Fuel Gauge [part_number=TOL-10617]
  PowerBoost = PowerBoost 500 Charger
  Arduino_Mega_2560 = Arduino Mega 2560 (Rev3)
  Board = female pin header, 4 pins [form="♀ (female)"]
  Switch = female pin header, 3 pins [form="♀ (female)"]
  On/Off = Toggle Switch [package=THT]

nets:
  N1: LiPo_Fuel_Gauge.SDA, Arduino_Mega_2560.D20/SDA, Arduino_Mega_2560.SDA, Board.pin3
  N2: LiPo_Fuel_Gauge.SCL, Arduino_Mega_2560.D21/SCL, Arduino_Mega_2560.SCL, Board.pin4
  GND: LiPo_Fuel_Gauge.QST, LiPo_Fuel_Gauge.GND, PowerBoost.GND, Arduino_Mega_2560.GND, Board.pin1, Switch.pin3, On/Off.L2
  N3: LiPo_Fuel_Gauge.VCC, PowerBoost.VBAT, Switch.pin1
  N4: PowerBoost.ENABLE, Switch.pin2, On/Off.COM
  N5: PowerBoost.5.0V, Arduino_Mega_2560.VIN, Board.pin2

custom parts:
  SparkFun LiPo Fuel Gauge: LiPo batteries are a great way to power your projects. They’re small, lightweight, and pack a pretty good punch for their size. Unfortunately, even the best batteries eventually run low on power and when they do it’s often unexpected (and at the worst time). Don’t be caught by surprise next time your board suddenly powers-down! The SparkFun LiPo Fuel Gauge connects your battery to your project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
  PowerBoost 500 Charger: The PowerBoost 500C is a little DC/DC boost converter module that can be powered by any 3.7V LiIon/LiPoly battery, and convert the battery output to 5.2V DC for running your 5V projects. At its heart is a TPS61090 boost converter from TI. This boost converter chip has some really nice extras such as low battery detection, 2A internal switch, synchronous conversion, excellent efficiency, and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
