# Fritzing sketch SensorModule (saved by Fritzing 0.9.3b)
breadboards: 1

parts:
  Part4 = Arduino Mega 2560 (Rev3)
  Part5 = Adafruit Bluefruit LE UART Friend [part_number="Adafruit #2479"]
  SparkFun_Pressure_Sensor_Breakout_-_MS5803-14BA2 = SparkFun Pressure Sensor Breakout - MS5803-14BA [part_number="SEN-12909 "]
  Part6 = Adafruit DS3231 [part_number="Adafruit #3013"]
  IR2 = TSOP312.., 314.. [package=THT]
  J6 = Piezo Speaker
  J7 = female pin header, 4 pins [form="♀ (female)"]
  J8 = female pin header, 4 pins [form="♀ (female)"]

nets:
  N1: Part4.D21/SCL, SparkFun_Pressure_Sensor_Breakout_-_MS5803-14BA2.SCL/SCLK, Part6.SCL, J8.pin4
  N2: Part4.D20/SDA, SparkFun_Pressure_Sensor_Breakout_-_MS5803-14BA2.SDA/SDI, Part6.SDA, J8.pin3
  N3: Part4.D19/RX1, Part5.TXO, J8.pin2
  N4: Part4.D18/TX1, Part5.RXI, J8.pin1
  VIN: Part4.3V3, Part5.VIN, SparkFun_Pressure_Sensor_Breakout_-_MS5803-14BA2.3.3V, Part6.Vin, IR2.Data, J7.pin1
  GND: Part4.GND, Part5.GND, Part5.CTS, SparkFun_Pressure_Sensor_Breakout_-_MS5803-14BA2.GND, Part6.GND, IR2.Vs, J6.pin1, J7.pin2
  N5: Part4.D2_PWM, J6.pin2, J7.pin4
  N6: Part4.D3_PWM, IR2.GND, J7.pin3

custom parts:
  Adafruit Bluefruit LE UART Friend: The Bluefruit LE UART Friend makes it easy to add Bluetooth Low Energy connectivity to anything with a hardware or software serial port. We even have nice hardware flow control so you won't have to think about losing data. Connect to your Arduino or other microcontroller or even just a standard FTDI cable for debugging and testing.
  SparkFun Pressure Sensor Breakout - MS5803-14BA: This is the MS5803-14BA Pressure Sensor Breakout, a high resolution pressure sensor with both an I2C and SPI interface. This MEMS pressure sensor measures the absolute pressure of the fluid around it which includes air, water, and anything else that acts like a viscous fluid. Depending on how you interpret the data, you can determine altitude, water depth, or any other tasks that require an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
  Adafruit DS3231: The datasheet for the DS3231 explains that this part is an "Extremely Accurate I²C-Integrated RTC/TCXO/Crystal". And, hey, it does exactly what it says on the tin! This Real Time Clock (RTC) is the most precise you can get in a small, low power package. Most RTCs use an external 32kHz timing crystal that is used to keep time with low current draw. And that's all well and good, but those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
