# Fritzing sketch DiveInoShield (saved by Fritzing 0.9.3b)
circuit board: 11cm x 6.5cm
breadboards: 1

parts:
  Microcontroller = Arduino Mega 2560 (Rev3)
  On/Off = Toggle Switch [package=THT]
  Bluefruit = Adafruit Bluefruit LE UART Friend [part_number="Adafruit #2479"]
  220k = Resistor [tolerance=±5% resistance=220k package=THT]
  22k = Resistor [tolerance=±5% resistance=22k package=THT]
  LED = LED - 5mm [color="Blue (430nm)" package="5 mm [THT]"]
  470 = Resistor [tolerance=±5% resistance=470 package=THT]
  Control = female pin header, 4 pins [form="♀ (female)"]
  10k = Resistor [tolerance=±5% resistance=10k package=THT]
  Reed = female pin header, 2 pins [form="♀ (female)"]
  470_2 = Resistor [tolerance=±5% resistance=470 package=THT]
  Fuel_Gauge = SparkFun LiPo Fuel Gauge [part_number=TOL-10617]
  Buzzer = Piezo Speaker - PC Mount [part_number=COM-07950]
  Infra = Infra red receiver
  Water = female pin header, 2 pins [form="♀ (female)"]
  NPN = NPN-Transistor [package="TO92 [THT]"]
  Data = female pin header, 4 pins [form="♀ (female)"]
  Pressure = SparkFun Pressure Sensor Breakout - MS5803-14BA [part_number="SEN-12909 "]
  Charger = PowerBoost 500 Charger
  RTC = Adafruit DS3231 [part_number="Adafruit #3013"]
  LCD = double row female pin header, 36 pins [form="♀ (female)"]  # not connected
  Power = female pin header, 6 pins [form="♀ (female)"]

nets:
  N1: Microcontroller.D21/SCL, Microcontroller.SCL, Fuel_Gauge.SCL, Data.pin4, Pressure.SCL/SCLK, RTC.SCL
  N2: Microcontroller.D20/SDA, Microcontroller.SDA, Fuel_Gauge.SDA, Data.pin3, Pressure.SDA/SDI, RTC.SDA
  N3: Microcontroller.D19/RX1, Bluefruit.TXO, Data.pin2
  N4: Microcontroller.D18/TX1, Bluefruit.RXI, Data.pin1
  GND: Microcontroller.GND, On/Off.L2, Bluefruit.GND, Bluefruit.CTS, 220k.Pin_0, LED.cathode, Reed.pin2, Fuel_Gauge.QST, Fuel_Gauge.GND, Buzzer.GND, Infra.GND, NPN.E, Pressure.GND, Charger.GND, RTC.GND, Power.pin4
  N5: Microcontroller.D11_PWM, 470.Pin_0, Control.pin1
  N6: Microcontroller.D10_PWM, Control.pin2, 470_2.Pin_1, NPN.C
  N7: Microcontroller.D9_PWM, Control.pin3, Infra.Data
  N8: Microcontroller.D8_PWM, Control.pin4, Buzzer.VCC
  VIN: Microcontroller.3V3, Bluefruit.VIN, 22k.Pin_0, 470_2.Pin_0, Infra.VCC, Pressure.3.3V, RTC.Vin, Power.pin2
  N9: Microcontroller.VIN, Charger.5.0V, Power.pin6
  N10: On/Off.COM, 10k.Pin_0, Reed.pin1, Charger.ENABLE
  N11: 220k.Pin_1, Water.pin1, NPN.B
  N12: 22k.Pin_1, Water.pin2
  N13: LED.anode, 470.Pin_1
  N14: 10k.Pin_1, Fuel_Gauge.VCC, Charger.VBAT

notes:
  DiveIno Shield
  SCL
  GND
  5V
  VIN
  VCC
  SND
  BAT
  EN
  IRD
  SDA
  TX1
  RX1
  RXI
  TXI
  CTS
  WTR
  LED
  QST
  Rev 01
  C
  B
  E

custom parts:
  Adafruit Bluefruit LE UART Friend: The Bluefruit LE UART Friend makes it easy to add Bluetooth Low Energy connectivity to anything with a hardware or software serial port. We even have nice hardware flow control so you won't have to think about losing data. Connect to your Arduino or other microcontroller or even just a standard FTDI cable for debugging and testing.
  SparkFun LiPo Fuel Gauge: LiPo batteries are a great way to power your projects. They’re small, lightweight, and pack a pretty good punch for their size. Unfortunately, even the best batteries eventually run low on power and when they do it’s often unexpected (and at the worst time). Don’t be caught by surprise next time your board suddenly powers-down! The SparkFun LiPo Fuel Gauge connects your battery to your project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
  Piezo Speaker - PC Mount: This is a small 12mm round speaker that operates around the audible 2kHz range. You can use these speakers to create simple music or user interfaces. Each speaker is PTH solderable and requires an operating voltage of 3.5-5V with a mean current of 35mA max. These speakers also have a typical sound output of 95 dBA and a coil resistance of 42 ±6.3 ohms.
  SparkFun Pressure Sensor Breakout - MS5803-14BA: This is the MS5803-14BA Pressure Sensor Breakout, a high resolution pressure sensor with both an I2C and SPI interface. This MEMS pressure sensor measures the absolute pressure of the fluid around it which includes air, water, and anything else that acts like a viscous fluid. Depending on how you interpret the data, you can determine altitude, water depth, or any other tasks that require an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
  PowerBoost 500 Charger: The PowerBoost 500C is a little DC/DC boost converter module that can be powered by any 3.7V LiIon/LiPoly battery, and convert the battery output to 5.2V DC for running your 5V projects. At its heart is a TPS61090 boost converter from TI. This boost converter chip has some really nice extras such as low battery detection, 2A internal switch, synchronous conversion, excellent efficiency, and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
  Adafruit DS3231: The datasheet for the DS3231 explains that this part is an "Extremely Accurate I²C-Integrated RTC/TCXO/Crystal". And, hey, it does exactly what it says on the tin! This Real Time Clock (RTC) is the most precise you can get in a small, low power package. Most RTCs use an external 32kHz timing crystal that is used to keep time with low current draw. And that's all well and good, but those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
