# Fritzing sketch WaterModule (saved by Fritzing 0.9.3b)
breadboards: 1

parts:
  Part2 = Arduino Mega 2560 (Rev3)
  Q2 = NPN-Transistor [package="TO92 [THT]"]
  LED2 = LED - 5mm [color="Blue (430nm)" package="5 mm [THT]"]
  R5 = Resistor [tolerance=±5% resistance=220 package=THT]
  R6 = Resistor [tolerance=±5% resistance=220 package=THT]
  R7 = Resistor [tolerance=±5% resistance=250k package=THT]
  R8 = Resistor [tolerance=±5% resistance=100k package=THT]
  J4 = female pin header, 2 pins [form="♀ (female)"]
  J5 = female pin header, 4 pins [form="♀ (female)"]

nets:
  N1: Part2.3V3, R6.Pin_0, R8.Pin_0, J5.pin4
  N2: Part2.GND, LED2.cathode, R7.Pin_0, J5.pin2
  N3: Part2.D6_PWM, Q2.E, R6.Pin_1, J5.pin3
  N4: Part2.D7_PWM, R5.Pin_0, J5.pin1
  N5: Q2.B, R7.Pin_1, J4.pin1
  N6: LED2.anode, R5.Pin_1
  N7: R8.Pin_1, J4.pin2

notes:
  Water module
